# Fritzing sketch atmega-16 (saved by Fritzing 0.8.3b)
breadboards: 1

parts:
  IC1 = ATmega16 [package="DIP (Dual Inline)"]
  Part1 = Arduino Uno (Rev3)
  LED1 = LED - 5mm [color="Red (633nm)" package="5 mm [THT]"]
  R1 = Resistor [tolerance=±5% resistance=220 package=THT]
  C1 = Electrolytic Capacitor [capacitance=10pF package="100 mil [THT, electrolytic]"]

nets:
  N1: IC1.PIN_6, Part1.ICSP_MOSI, Part1.D11_PWM/MOSI
  N2: IC1.PIN_7, Part1.ICSP_MISO, Part1.D12/MISO
  N3: IC1.PIN_8, Part1.ICSP_SCK, Part1.D13/SCK
  N4: IC1.PIN_9, Part1.D10_PWM/SS
  N5: IC1.PIN_10, Part1.5V
  N6: IC1.PIN_11, IC1.PIN_31, Part1.GND, R1.Pin_1, C1.-
  N7: IC1.PIN_20, LED1.anode
  N8: Part1.RESET, C1.+
  N9: LED1.cathode, R1.Pin_0

custom parts:
  ATmega16: ATmega16 - 40 pins, 600 mil dual inline package (DIP)
